// Logisim project Exercicio 2.circ as structural Verilog: 2 circuits, main circuit Exercicio 2 (Completo)
module Exercicio_2__Completo (
  input  in_1,
  input  A,
  input  B,
  input  C,
  input  D,
  output Qa,
  output Qb,
  output Qc,
  output Qd
);

  wire and_1_out, and_2_out, clock_1_out, pull_resistor_1_node, pull_resistor_2_node, pull_resistor_3_node,
       pull_resistor_4_node;

  Pull_Resistor #(.pull(1)) pull_resistor_1 (.node(pull_resistor_1_node));
  Pull_Resistor #(.pull(1)) pull_resistor_2 (.node(pull_resistor_2_node));
  Pull_Resistor #(.pull(1)) pull_resistor_3 (.node(pull_resistor_3_node));
  Pull_Resistor pull_resistor_4 (.node(pull_resistor_4_node));
  and and_1 (and_1_out, B, C);
  and and_2 (and_2_out, B, C);
  J_K_Flip_Flop FFJKA (.J(and_1_out), .clk(clock_1_out), .K(and_2_out), .Q(Qa), .reset(in_1));  // open: Qn, preset, en
  J_K_Flip_Flop FFJKB (.J(C), .clk(clock_1_out), .K(C), .Q(Qb), .reset(in_1));  // open: Qn, preset, en
  J_K_Flip_Flop FFJKC (
    .J(pull_resistor_1_node), .clk(clock_1_out), .K(pull_resistor_2_node), .Q(Qc), .reset(in_1));  // open: Qn, preset, en
  J_K_Flip_Flop FFJKD (
    .J(pull_resistor_3_node), .clk(clock_1_out), .K(pull_resistor_4_node), .Q(Qd), .preset(in_1));  // open: Qn, en, reset
  Clock clock_1 (.out(clock_1_out));
endmodule

module Exercicio_2__Saidas_Simples (
  input  A,
  input  B,
  input  C,
  input  D,
  output J3,
  output K3,
  output J2,
  output K2,
  output J1,
  output K1,
  output J0,
  output K0
);

  Pull_Resistor #(.pull(1)) pull_resistor_1 (.node(J1));
  Pull_Resistor #(.pull(1)) pull_resistor_2 (.node(K1));
  Pull_Resistor #(.pull(1)) pull_resistor_3 (.node(J0));
  Pull_Resistor pull_resistor_4 (.node(K0));
  and and_1 (J3, B, C);
  and and_2 (K3, B, C);

  assign J2 = C;
  assign K2 = C;
endmodule
