// Logisim project Exercicio 3.circ as structural Verilog: 2 circuits, main circuit Exercicio 3 (Completo)
module Exercicio_3__Completo (
  input  in_1,
  input  A,
  input  B,
  input  C,
  output out_5,
  output out_6,
  output out_7
);

  wire clock_1_out, not_1_out, not_2_out, not_3_out, not_4_out, or_1_out;

  not not_1 (not_1_out, B);
  not not_2 (not_2_out, C);
  or or_1 (or_1_out, C, not_3_out);
  not not_3 (not_3_out, A);
  not not_4 (not_4_out, A);
  Clock clock_1 (.out(clock_1_out));
  J_K_Flip_Flop j_k_ff_1 (
    .J(not_1_out), .clk(clock_1_out), .K(not_2_out), .Q(out_5), .preset(in_1));  // open: Qn, en, reset
  J_K_Flip_Flop j_k_ff_2 (.J(C), .clk(clock_1_out), .K(or_1_out), .Q(out_6), .reset(in_1));  // open: Qn, preset, en
  J_K_Flip_Flop j_k_ff_3 (.J(not_4_out), .clk(clock_1_out), .K(A), .Q(out_7), .preset(in_1));  // open: Qn, en, reset
endmodule

module Exercicio_3__Saidas_Simples (
  input  A,
  input  B,
  input  C,
  output J2,
  output K2,
  output J1,
  output K1,
  output J0,
  output K0
);

  wire not_3_out;

  not not_1 (J2, B);
  not not_2 (K2, C);
  or or_1 (K1, C, not_3_out);
  not not_3 (not_3_out, A);
  not not_4 (J0, A);

  assign J1 = C;
  assign K0 = A;
endmodule
