// Logisim project Exercicio 1.circ as structural Verilog: 2 circuits, main circuit Exercicio 1 (Completo)
module Exercicio_1__Completo (
  input  in_1,
  input  A,
  input  B,
  input  C,
  output out_5,
  output out_6,
  output out_7
);

  wire and_1_out, and_2_out, and_3_out, and_4_out, clock_1_out, not_1_out, not_2_out, not_3_out, not_4_out,
       or_1_out, or_2_out, pull_resistor_1_node, pull_resistor_2_node;

  and and_1 (and_1_out, B, C);
  and and_2 (and_2_out, B, C);
  not not_1 (not_1_out, A);
  not not_2 (not_2_out, C);
  not not_3 (not_3_out, A);
  not not_4 (not_4_out, B);
  Pull_Resistor #(.pull(1)) pull_resistor_1 (.node(pull_resistor_1_node));
  Pull_Resistor #(.pull(1)) pull_resistor_2 (.node(pull_resistor_2_node));
  and and_3 (and_3_out, not_1_out, not_2_out);
  and and_4 (and_4_out, A, C);
  or or_1 (or_1_out, not_3_out, not_4_out);
  or or_2 (or_2_out, and_3_out, and_4_out);
  Clock clock_1 (.out(clock_1_out));
  J_K_Flip_Flop j_k_ff_1 (
    .J(and_1_out), .clk(clock_1_out), .K(and_2_out), .Q(out_5), .reset(in_1));  // open: Qn, preset, en
  J_K_Flip_Flop j_k_ff_2 (
    .J(or_2_out), .clk(clock_1_out), .K(or_1_out), .Q(out_6), .preset(in_1));  // open: Qn, en, reset
  J_K_Flip_Flop j_k_ff_3 (
    .J(pull_resistor_1_node), .clk(clock_1_out), .K(pull_resistor_2_node), .Q(out_7), .preset(in_1));  // open: Qn, en, reset
endmodule

module Exercicio_1__Saidas_Simples (
  input  A,
  input  B,
  input  C,
  output Aj,
  output Ak,
  output Bj,
  output Bk,
  output Cj,
  output Ck
);

  wire and_3_out, and_4_out, not_1_out, not_2_out, not_3_out, not_4_out;

  and and_1 (Aj, B, C);
  and and_2 (Ak, B, C);
  not not_1 (not_1_out, A);
  not not_2 (not_2_out, C);
  not not_3 (not_3_out, A);
  not not_4 (not_4_out, B);
  Pull_Resistor #(.pull(1)) pull_resistor_1 (.node(Cj));
  Pull_Resistor #(.pull(1)) pull_resistor_2 (.node(Ck));
  and and_3 (and_3_out, not_1_out, not_2_out);
  and and_4 (and_4_out, A, C);
  or or_1 (Bk, not_3_out, not_4_out);
  or or_2 (Bj, and_3_out, and_4_out);
endmodule
